# Fritzing sketch pcbv2 (saved by Fritzing 0.9.10b)
circuit board: 2.83586cm x 6.5123cm

parts:
  A1 = ESP32-C6 supermini
  J1 = Screw terminal - 2 pins [package=THT]
  OLED1 = OLED 128x64 I2C Monochrome Display GND-VDD

nets:
  N1: A1.GP1, OLED1.SDA
  N2: A1.GP2, OLED1.SCK
  3V3: A1.3V3, OLED1.VDD
  GND: A1.GND, J1.pin2, OLED1.GND
  N3: A1.5V, J1.pin1

notes:
  + -

custom parts:
  ESP32-C6 supermini: TZT SuperMini ESP32-C6 WiFi+Bluetooth ESP32 Development Board.
  OLED 128x64 I2C Monochrome Display GND-VDD: OLED 128x64 I2C Monochrome Display. Note: there are two variants of this part, this one is the GND VDD SCK SDA variant. The other is VDD GND SCK SDA. Make sure you select the part that matches your module as using the incorrect part will probably destroy your module! In addition the mounting holes are marked on silkscreen but not by default drilled. If you want drilled mounting holes, copy a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
